# Fritzing sketch c6 (saved by Fritzing 0.9.3b)
breadboards: 1

parts:
  Raspberry_Pi_1 = Raspberry Pi 3 [part_number=RPI-3-V1.2]
  DHT1 = DHT11 Humitidy and Temperature Sensor
  R5 = Resistor [tolerance=±5% resistance=4.7k package=THT]

nets:
  3V3: Raspberry_Pi_1.3v3, DHT1.VDD, R5.Pin_0
  N1: Raspberry_Pi_1.GPIO25, DHT1.DATA, R5.Pin_1
  GND: Raspberry_Pi_1.GND, DHT1.GND

notes:
  Circuito 6

custom parts:
  DHT11 Humitidy and Temperature Sensor: DHT11 Humidity and Temperature Sensor
